// Logisim project 8bit.circ as structural Verilog: 1 circuit, main circuit main
module main (
  input  Reset,
  input  [7:0] in_2
);

  wire ADD, AI, and_1_out, AO, BI, buffer_1_out, CE, CLK, clock_1_out, CMP, CO, counter_2_carry, CR, HLT, II,
       IO, J, MI, MO, not_1_out, OI, or_1_out, SUB;
  wire [2:0] comparator_1_gt;
  wire [3:0] controlled_buffer_9_out, counter_1_q, counter_3_q, register_1_q;
  wire [4:0] pull_resistor_13_node;
  wire [7:0] adder_1_out, BUS, controlled_buffer_2_out, register_2_q, register_3_q, rom_2_data, rom_3_data,
       rom_4_data, rom_5_data, subtractor_1_out;
  wire [7:4] register_1_q_2;

  Counter #(.width(4), .max('hf)) counter_1 (
    .Q(counter_1_q), .clk(CLK), .clr(or_1_out));  // open: load, D, count, carry
  Pull_Resistor pull_resistor_1 (.node(IO));
  assign BUS[3:0] = IO ? register_1_q : 4'bz;  // Controlled_Buffer controlled_buffer_1
  Register #(.trigger("falling")) register_1 (
    .D(BUS), .en(II), .Q({register_1_q_2, register_1_q}), .clk(CLK), .clr(or_1_out));
  Pull_Resistor pull_resistor_2 (.node(II));
  or or_1 (or_1_out, Reset, CR);
  Pull_Resistor pull_resistor_3 (.node(CR));
  ROM #(.dataWidth(16)) rom_1 (
    .addr({register_1_q_2, counter_1_q}),
    .data({HLT, J, CO, CE, MI, MO, AI, AO, BI, OI, SUB, ADD, II, IO, CR, CMP}));  // open: sel
  Counter #(.width(1), .max('h1)) counter_2 (
    .carry(counter_2_carry), .clk(and_1_out), .clr(Reset));  // open: load, D, count, Q
  Pull_Resistor pull_resistor_4 (.node(J));
  not not_1 (not_1_out, J);
  and and_1 (and_1_out, CE, buffer_1_out);
  Pull_Resistor pull_resistor_5 (.node(CE));
  Pull_Resistor pull_resistor_6 (.node(OI));
  Pull_Resistor pull_resistor_7 (.node(Reset));
  Pull_Resistor pull_resistor_8 (.node(CO));
  Counter #(.width(4), .max('hf)) counter_3 (
    .load(J), .D(BUS[3:0]), .count(not_1_out), .Q(counter_3_q), .clk(counter_2_carry), .clr(Reset));  // open: carry
  buf buffer_1 (buffer_1_out, CLK);
  assign controlled_buffer_2_out = OI ? BUS : 8'bz;  // Controlled_Buffer controlled_buffer_2
  assign controlled_buffer_2_out = Reset ? in_2 : 8'bz;  // Controlled_Buffer controlled_buffer_3
  assign BUS[3:0] = CO ? counter_3_q : 4'bz;  // Controlled_Buffer controlled_buffer_4
  Pull_Resistor pull_resistor_9 (.node(AI));
  Pull_Resistor pull_resistor_10 (.node(BI));
  _7_Segment_Display u_7_segment_display_1 (
    .g(rom_2_data[7]), .f(rom_2_data[6]), .a(rom_2_data[5]), .b(rom_2_data[4]), .e(rom_2_data[0]),
    .d(rom_2_data[1]), .c(rom_2_data[2]), .dp(rom_2_data[3]));
  Pull_Resistor pull_resistor_11 (.node(AO));
  assign BUS = AO ? register_2_q : 8'bz;  // Controlled_Buffer controlled_buffer_5
  Register #(.trigger("falling")) register_2 (.D(BUS), .en(AI), .Q(register_2_q), .clk(CLK), .clr(Reset));
  Register #(.trigger("falling")) register_3 (.D(BUS), .en(BI), .Q(register_3_q), .clk(CLK), .clr(Reset));
  ROM rom_2 (.addr(controlled_buffer_2_out), .data(rom_2_data));  // open: sel
  _7_Segment_Display u_7_segment_display_2 (
    .g(rom_3_data[7]), .f(rom_3_data[6]), .a(rom_3_data[5]), .b(rom_3_data[4]), .e(rom_3_data[0]),
    .d(rom_3_data[1]), .c(rom_3_data[2]), .dp(rom_3_data[3]));
  Pull_Resistor pull_resistor_12 (.node(BUS));
  assign BUS = ADD ? adder_1_out : 8'bz;  // Controlled_Buffer controlled_buffer_6
  Adder adder_1 (.a(register_2_q), .b(register_3_q), .out(adder_1_out));  // open: cin, cout
  Subtractor subtractor_1 (.a(register_2_q), .b(register_3_q), .out(subtractor_1_out));  // open: bin, bout
  Comparator comparator_1 (
    .a(register_2_q), .b(register_3_q), .gt(comparator_1_gt[0]), .eq(comparator_1_gt[1]),
    .lt(comparator_1_gt[2]));
  Pull_Resistor pull_resistor_13 (.node(pull_resistor_13_node));
  _7_Segment_Display u_7_segment_display_3 (
    .g(rom_5_data[7]), .f(rom_5_data[6]), .a(rom_5_data[5]), .b(rom_5_data[4]), .e(rom_5_data[0]),
    .d(rom_5_data[1]), .c(rom_5_data[2]), .dp(rom_5_data[3]));
  Pull_Resistor pull_resistor_14 (.node(ADD));
  assign BUS = SUB ? subtractor_1_out : 8'bz;  // Controlled_Buffer controlled_buffer_7
  Pull_Resistor pull_resistor_15 (.node(SUB));
  assign BUS = CMP ? {pull_resistor_13_node, comparator_1_gt} : 8'bz;  // Controlled_Buffer controlled_buffer_8
  Pull_Resistor pull_resistor_16 (.node(CMP));
  ROM rom_3 (.addr(controlled_buffer_2_out), .data(rom_3_data));  // open: sel
  Pull_Resistor pull_resistor_17 (.node(MI));
  assign controlled_buffer_9_out = MI ? BUS[3:0] : 4'bz;  // Controlled_Buffer controlled_buffer_9
  Clock clock_1 (.out(clock_1_out));
  Pull_Resistor pull_resistor_18 (.node(HLT));
  and and_2 (CLK, clock_1_out, ~HLT);  // AND_Gate
  ROM #(.addrWidth(4)) rom_4 (.addr(controlled_buffer_9_out), .data(rom_4_data));  // open: sel
  ROM rom_5 (.addr(controlled_buffer_2_out), .data(rom_5_data));  // open: sel
  assign BUS = MO ? rom_4_data : 8'bz;  // Controlled_Buffer controlled_buffer_10
  Pull_Resistor pull_resistor_19 (.node(MO));

  // Other names for the same wires on the sheet: CLR = Reset

  // Notes on the sheet:
  //   Reg A, Reg B and ALU
  //   Instruction Reader
  //   contents of rom_1 (hex, n*v repeats v):
  //   2800 1408 13*0 2 2800 1408 804 600 2 11*0 2800 1408 210 2 12*0 2800 1408 220 2 12*0 2800 1408 180 2
  //   12*0 2800 1408 201 2 12*0 2800 1408 804 480 2 11*0 2800 1408 8000 13*0 2800 1408 8000 13*0 2800 1408
  //   8000 13*0 2800 1408 8000 13*0 2800 1408 4004 2 12*0 2800 1408 804 440 2 11*0 2800 1408 40 2 12*0
  //   2800 1408 140 2 12*0 8000
  //   Program Counter
  //   contents of rom_2 (hex, n*v repeats v):
  //   100*77 100*14 56*b3
  //   contents of rom_3 (hex, n*v repeats v):
  //   10*77 10*14 10*b3 10*b6 10*d4 10*e6 10*e7 10*34 10*f7 10*f6 10*77 10*14 10*b3 10*b6 10*d4 10*e6
  //   10*e7 10*34 10*f7 10*f6 10*77 10*14 10*b3 10*b6 10*d4 6*e6
  //   RAM
  //   CLOCK
  //   OUTPUT
  //   contents of rom_4 (hex, n*v repeats v):
  //   1b 6c 20 40 e0 50 e0 1d 30 e0 f0 14 37 63
  //   contents of rom_5 (hex, n*v repeats v):
  //   77 14 b3 b6 d4 e6 e7 34 f7 f6 77 14 b3 b6 d4 e6 e7 34 f7 f6 77 14 b3 b6 d4 e6 e7 34 f7 f6 77 14 b3
  //   b6 d4 e6 e7 34 f7 f6 77 14 b3 b6 d4 e6 e7 34 f7 f6 77 14 b3 b6 d4 e6 e7 34 f7 f6 77 14 b3 b6 d4 e6
  //   e7 34 f7 f6 77 14 b3 b6 d4 e6 e7 34 f7 f6 77 14 b3 b6 d4 e6 e7 34 f7 f6 77 14 b3 b6 d4 e6 e7 34 f7
  //   f6 77 14 b3 b6 d4 e6 e7 34 f7 f6 77 14 b3 b6 d4 e6 e7 34 f7 f6 77 14 b3 b6 d4 e6 e7 34 f7 f6 77 14
  //   b3 b6 d4 e6 e7 34 f7 f6 77 14 b3 b6 d4 e6 e7 34 f7 f6 77 14 b3 b6 d4 e6 e7 34 f7 f6 77 14 b3 b6 d4
  //   e6 e7 34 f7 f6 77 14 b3 b6 d4 e6 e7 34 f7 f6 77 14 b3 b6 d4 e6 e7 34 f7 f6 77 14 b3 b6 d4 e6 e7 34
  //   f7 f6 77 14 b3 b6 d4 e6 e7 34 f7 f6 77 14 b3 b6 d4 e6 e7 34 f7 f6 77 14 b3 b6 d4 e6 e7 34 f7 f6 77
  //   14 b3 b6 d4 e6 e7 34 f7 f6 77 14 b3 b6 d4 e6 e7 34 f7 f6 77 14 b3 b6 d4 e6
endmodule
